# Fritzing sketch circuito (saved by Fritzing 0.8.3b)
breadboards: 1

parts:
  Parte1 = Arduino Uno (Rev3)
  U1 = LCD-16X2 [package=lcd-16x2]  # not connected
  R1 = Rotary Potentiometer (Small)
  R2 = Resistor [tolerance=±5% resistance=220 package=THT]
  T1 = LM35 Temperature Sensor [package="TO92 [THT]"]
  LED1 = RGB LED (com. anode, rbg) [package="5 mm [THT]"]

nets:
  N1: Parte1.A0, T1.Vout
  N2: Parte1.D8, LED1.green_cathode
  N3: Parte1.D9_PWM, LED1.blue_cathode
  N4: Parte1.D10_PWM/SS, LED1.red_cathode
  N5: Parte1.D7, R1.wiper
  N6: R1.leg1, T1.+Vs
  N7: R1.leg2, R2.Pin_1, T1.GND
  N8: R2.Pin_0, LED1.common_anode
